// Logisim project cs120_2bitdecoder.circ as structural Verilog: 1 circuit, main circuit main
module main (
  input  A,
  input  B,
  output out_3,
  output out_4,
  output out_5,
  output out_6
);

  and and_1 (out_3, ~A, ~B);  // AND_Gate
  and and_2 (out_4, ~A, B);  // AND_Gate
  and and_3 (out_5, A, ~B);  // AND_Gate
  and and_4 (out_6, A, B);

  // Notes on the sheet:
  //   Satvik Kukreti
endmodule
