// Logisim project cs120_mux.circ as structural Verilog: 1 circuit, main circuit main
module main (
  input  S,
  input  D0,
  input  D1,
  output Y
);

  wire and_1_out, and_2_out;

  and and_1 (and_1_out, ~S, D0);  // AND_Gate
  and and_2 (and_2_out, S, D1);
  or or_1 (Y, and_1_out, and_2_out);

  // Notes on the sheet:
  //   Satvik Kukreti
endmodule
