// Logisim project cs120_q5.circ as structural Verilog: 1 circuit, main circuit main
module main (
  input  A,
  input  B,
  input  C,
  input  D,
  output out_5
);

  wire and_1_out, and_2_out;

  and and_1 (and_1_out, A, ~D);  // AND_Gate
  and and_2 (and_2_out, B, C, D);
  or or_1 (out_5, and_1_out, and_2_out);

  // Notes on the sheet:
  //   Satvik Kukreti
  //   Boolean Equation: A!D + BCD
endmodule
